# Fritzing sketch Angela Davies (saved by Fritzing 0.9.3b)

parts:
  M1 = DC Motor
  Part1 = Arduino Uno (Rev3)  # not connected
  Part2 = Adafruit Motor/Stepper/Servo Shield [part_number="Adafruit #1438"]
  Power_plug1 = Power plug
  LED6 = LED - 5mm [color="White (6500K)" package="5 mm [THT]"]
  LED1 = LED - 5mm [color="White (6500K)" package="5 mm [THT]"]
  LED8 = LED - 5mm [color="White (6500K)" package="5 mm [THT]"]
  LED9 = LED - 5mm [color="White (6500K)" package="5 mm [THT]"]
  LED10 = LED - 5mm [color="White (6500K)" package="5 mm [THT]"]
  R1 = Resistor [tolerance=±5% resistance=220 package=THT]
  LED11 = LED - 5mm [color="White (6500K)" package="5 mm [THT]"]
  LED12 = LED - 5mm [color="White (6500K)" package="5 mm [THT]"]
  LED13 = LED - 5mm [color="White (6500K)" package="5 mm [THT]"]
  LED14 = LED - 5mm [color="White (6500K)" package="5 mm [THT]"]
  LED6_2 = LED - 5mm [color="White (6500K)" package="5 mm [THT]"]
  R2 = Resistor [tolerance=±5% resistance=220 package=THT]

nets:
  GND: M1.pin_1, Part2.GND, Power_plug1.GND, LED6.anode, LED1.anode, LED8.anode, LED9.anode, LED10.anode, LED11.anode, LED12.anode, LED13.anode, LED14.anode, LED6_2.anode
  N1: M1.pin_2, Part2.M1A
  N2: Part2.VMOTOR, Power_plug1.VCC
  N3: Part2.D9, R2.Pin_1
  N4: Part2.D10, R1.Pin_1
  N5: LED6.cathode, LED1.cathode, LED8.cathode, LED9.cathode, LED10.cathode, R1.Pin_0
  N6: LED11.cathode, LED12.cathode, LED13.cathode, LED14.cathode, LED6_2.cathode, R2.Pin_0

notes:
  Angela Davies, 1.0
  The Shield is plugged on top of the Arduino its just here for reference.

custom parts:
  Adafruit Motor/Stepper/Servo Shield: The original Adafruit Motorshield kit is one of our most beloved kits, which is why we decided to make something even better. We have upgraded the shield kit to make the bestest, easiest way to drive DC and Stepper motors. This shield will make quick work of your next robotics project! We kept the ability to drive up to 4 DC motors or 2 stepper motors, but added many improvements: Instead of a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
